// Logisim project pc.circ as structural Verilog: 5 circuits, main circuit main
module main (
  input  in_1
);

  wire bit_extender_1_out, clock_1_out;
  wire [4:0] bit_extender_2_out;
  wire [11:0] processor_1_out_4;
  wire [15:0] rom_1_data, screenadd, screenen;
  wire [31:0] processor_1_s1, screenbuffer_1_out_6, screenbuffer_1_out_7, screenbuffer_1_out_8,
       screenbuffer_1_out_9, screenbuffer_1_out_10, screenbuffer_1_out_11, screenbuffer_1_out_12,
       screenbuffer_1_out_13, screenbuffer_1_out_14, screenbuffer_1_out_15, screenbuffer_1_out_16,
       screenbuffer_1_out_17, screenbuffer_1_out_18, screenbuffer_1_out_19, screenbuffer_1_out_20,
       screenbuffer_1_out_21, screenbuffer_1_out_22, screenbuffer_1_out_23, screenbuffer_1_out_24,
       screenbuffer_1_out_25, screenbuffer_1_out_26, screenbuffer_1_out_27, screenbuffer_1_out_28,
       screenbuffer_1_out_29, screenbuffer_1_out_30, screenbuffer_1_out_31, screenbuffer_1_out_32,
       screenbuffer_1_out_33, screenbuffer_1_out_34, screenbuffer_1_out_35, screenbuffer_1_out_36,
       screenbuffer_1_out_37;

  DotMatrix #(.matrixcols(32), .matrixrows(32), .persist(64)) dotmatrix_1 (
    .col0(screenbuffer_1_out_6), .col1(screenbuffer_1_out_7), .col2(screenbuffer_1_out_8),
    .col3(screenbuffer_1_out_9), .col4(screenbuffer_1_out_10), .col5(screenbuffer_1_out_11),
    .col6(screenbuffer_1_out_12), .col7(screenbuffer_1_out_13), .col8(screenbuffer_1_out_14),
    .col9(screenbuffer_1_out_15), .col10(screenbuffer_1_out_16), .col11(screenbuffer_1_out_17),
    .col12(screenbuffer_1_out_18), .col13(screenbuffer_1_out_19), .col14(screenbuffer_1_out_20),
    .col15(screenbuffer_1_out_21), .col16(screenbuffer_1_out_37), .col17(screenbuffer_1_out_36),
    .col18(screenbuffer_1_out_35), .col19(screenbuffer_1_out_34), .col20(screenbuffer_1_out_33),
    .col21(screenbuffer_1_out_32), .col22(screenbuffer_1_out_31), .col23(screenbuffer_1_out_30),
    .col24(screenbuffer_1_out_29), .col25(screenbuffer_1_out_28), .col26(screenbuffer_1_out_27),
    .col27(screenbuffer_1_out_26), .col28(screenbuffer_1_out_25), .col29(screenbuffer_1_out_24),
    .col30(screenbuffer_1_out_23), .col31(screenbuffer_1_out_22));
  screenbuffer screenbuffer_1 (
    .Address(bit_extender_2_out), .data(processor_1_s1), .enable(bit_extender_1_out), .clock(clock_1_out),
    .clear(in_1), .out_6(screenbuffer_1_out_6), .out_7(screenbuffer_1_out_7), .out_8(screenbuffer_1_out_8),
    .out_9(screenbuffer_1_out_9), .out_10(screenbuffer_1_out_10), .out_11(screenbuffer_1_out_11),
    .out_12(screenbuffer_1_out_12), .out_13(screenbuffer_1_out_13), .out_14(screenbuffer_1_out_14),
    .out_15(screenbuffer_1_out_15), .out_16(screenbuffer_1_out_16), .out_17(screenbuffer_1_out_17),
    .out_18(screenbuffer_1_out_18), .out_19(screenbuffer_1_out_19), .out_20(screenbuffer_1_out_20),
    .out_21(screenbuffer_1_out_21), .out_22(screenbuffer_1_out_22), .out_23(screenbuffer_1_out_23),
    .out_24(screenbuffer_1_out_24), .out_25(screenbuffer_1_out_25), .out_26(screenbuffer_1_out_26),
    .out_27(screenbuffer_1_out_27), .out_28(screenbuffer_1_out_28), .out_29(screenbuffer_1_out_29),
    .out_30(screenbuffer_1_out_30), .out_31(screenbuffer_1_out_31), .out_32(screenbuffer_1_out_32),
    .out_33(screenbuffer_1_out_33), .out_34(screenbuffer_1_out_34), .out_35(screenbuffer_1_out_35),
    .out_36(screenbuffer_1_out_36), .out_37(screenbuffer_1_out_37));
  Bit_Extender #(.in_width(16), .out_width(1)) bit_extender_1 (.in(screenen), .out(bit_extender_1_out));
  Bit_Extender #(.in_width(16), .out_width(5)) bit_extender_2 (.in(screenadd), .out(bit_extender_2_out));
  ROM #(.addrWidth(12), .dataWidth(16)) rom_1 (.addr(processor_1_out_4), .data(rom_1_data));  // open: sel
  Clock clock_1 (.out(clock_1_out));
  Processor processor_1 (
    .clock(clock_1_out), .ins(rom_1_data), .out_4(processor_1_out_4), .reset(in_1),
    .S1(processor_1_s1[15:0]), .S2(processor_1_s1[31:16]), .SA(screenadd), .SE(screenen));

  // Notes on the sheet:
  //   contents of rom_1 (hex, n*v repeats v):
  //   8c80 8061 8082 80a3 b009 8c80 b03d f007 81f9 803a a722 e01d 2722 3359 803b 2360 805c 283c 2361 801d
  //   287c 23a3 23bb 735b a77d 237c d018 f01e f01e ac00 ac00 a200 a221 a242 a263 a284 a010 a031 a052 a073
  //   b009 a010 a031 a052 2044 a073 b009 ac00 8001 8002 8023 8804 2080 7020 2003 a480 d038 ac00 801c 801d
  //   801e 9d5f 811e 33fe 8c1e 23fe 801e 23df 23bf 239f 803b 23bb 23db 23db 23fb 23fb 23fb 737f 801a 8419
  //   735e 5020 703c 201b 5020 703d 201b 235b a759 d053 801b 737f ac00 9461 9fe2 8103 9fe4 8c80 8ca5 9446
  //   8027 8cc9 942a 804b 944c 8cad 900e 31c3 3043 2044 7041 7040 7045 7046 70e9 212b a52c d075 71ca 254b
  //   a54d d079 b03d ac00
endmodule

module ULA (
  input  [15:0] A,
  input  [3:0] F,
  input  [15:0] B,
  output [15:0] R,
  output FG,
  output FE
);

  wire or_1_out, or_2_out, or_3_out, or_4_out, or_5_out, or_6_out, or_7_out, or_8_out, or_9_out, or_10_out,
       or_11_out, or_12_out, or_13_out, or_14_out, or_15_out, or_16_out, or_17_out, or_18_out, or_19_out,
       or_20_out, or_21_out, or_22_out, or_23_out, or_24_out;
  wire [15:0] and_2_out, and_3_out, and_4_out, and_5_out, and_6_out, and_7_out, and_8_out, and_9_out,
       and_10_out, resltado_divisao, resultado_and, resultado_left_shift, resultado_multicacao,
       resultado_not, resultado_or, resultado_right_shift, resultado_soma, resultado_subtracao;
  wire [15:15] not_1_out, not_2_out, not_3_out, not_4_out, not_5_out, not_6_out, not_7_out, not_8_out;

  buf or_1 (or_1_out, F[2]);  // OR_Gate OR_Gate
  buf or_2 (or_2_out, F[2]);  // OR_Gate OR_Gate
  or or_3 (or_3_out, F[2], ~F[3]);  // OR_Gate
  or or_4 (or_4_out, ~F[2], ~F[3]);  // OR_Gate
  buf or_5 (or_5_out, ~F[2]);  // OR_Gate OR_Gate
  buf or_6 (or_6_out, ~F[2]);  // OR_Gate OR_Gate
  or or_7 (or_7_out, ~F[2], ~F[3]);  // OR_Gate
  or or_8 (or_8_out, F[0], F[1]);
  or or_9 (or_9_out, or_8_out, or_10_out);
  or or_10 (or_10_out, F[2], ~F[3]);  // OR_Gate
  or or_11 (or_11_out, ~F[0], F[1]);  // OR_Gate
  or or_12 (or_12_out, or_11_out, or_1_out);
  or or_13 (or_13_out, F[0], ~F[1]);  // OR_Gate
  or or_14 (or_14_out, or_13_out, or_2_out);
  or or_15 (or_15_out, ~F[0], ~F[1]);  // OR_Gate
  or or_16 (or_16_out, or_15_out, or_3_out);
  or or_17 (or_17_out, F[0], ~F[1]);  // OR_Gate
  or or_18 (or_18_out, or_17_out, or_4_out);
  or or_19 (or_19_out, ~F[0], ~F[1]);  // OR_Gate
  or or_20 (or_20_out, or_19_out, or_5_out);
  or or_21 (or_21_out, F[0], F[1]);
  or or_22 (or_22_out, or_21_out, or_6_out);
  or or_23 (or_23_out, ~F[0], F[1]);  // OR_Gate
  or or_24 (or_24_out, or_23_out, or_7_out);
  not not_1 (not_1_out[15], or_9_out);
  not not_2 (not_2_out[15], or_12_out);
  not not_3 (not_3_out[15], or_14_out);
  not not_4 (not_4_out[15], or_16_out);
  not not_5 (not_5_out[15], or_18_out);
  not not_6 (not_6_out[15], or_20_out);
  not not_7 (not_7_out[15], or_22_out);
  not not_8 (not_8_out[15], or_24_out);
  Adder #(.width(16)) adder_1 (.a(A), .b(B), .out(resultado_soma));  // open: cin, cout
  Subtractor #(.width(16)) subtractor_1 (.a(A), .b(B), .out(resultado_subtracao));  // open: bin, bout
  Multiplier #(.width(16)) multiplier_1 (.a(A), .b(B), .out(resultado_multicacao));  // open: cin, cout
  Divider #(.width(16)) divider_1 (.a(A), .b(B), .out(resltado_divisao));  // open: upper, rem
  assign resultado_and = A & B;  // AND_Gate and_1, 16 bits wide
  assign resultado_or = A | B;  // OR_Gate or_25, 16 bits wide
  assign resultado_not = ~A;  // NOT_Gate not_9, 16 bits wide
  Shifter #(.width(16)) shifter_1 (.in(A), .\dist (B[3:0]), .out(resultado_left_shift));
  Shifter #(.width(16), .shift("lr")) shifter_2 (.in(A), .\dist (B[3:0]), .out(resultado_right_shift));
  Comparator #(.width(16), .mode("unsigned")) comparator_1 (.a(A), .b(B), .gt(FG), .eq(FE));  // open: lt
  assign and_2_out = {16{not_1_out[15]}} & resultado_soma;  // AND_Gate and_2, 16 bits wide
  assign and_3_out = {16{not_2_out[15]}} & resultado_subtracao;  // AND_Gate and_3, 16 bits wide
  assign and_4_out = {16{not_3_out[15]}} & resultado_multicacao;  // AND_Gate and_4, 16 bits wide
  assign and_5_out = {16{not_4_out[15]}} & resltado_divisao;  // AND_Gate and_5, 16 bits wide
  assign and_6_out = {16{not_5_out[15]}} & resultado_and;  // AND_Gate and_6, 16 bits wide
  assign and_7_out = {16{not_6_out[15]}} & resultado_or;  // AND_Gate and_7, 16 bits wide
  assign and_8_out = {16{1'b0}} & resultado_not;  // AND_Gate and_8, 16 bits wide
  assign and_9_out = {16{not_7_out[15]}} & resultado_left_shift;  // AND_Gate and_9, 16 bits wide
  assign and_10_out = {16{not_8_out[15]}} & resultado_right_shift;  // AND_Gate and_10, 16 bits wide
  assign R = and_2_out | and_3_out | and_4_out | and_5_out | and_6_out | and_7_out | and_8_out | and_9_out | and_10_out;  // OR_Gate or_26, 16 bits wide

  // Other names for the same wires on the sheet: b0 = F[0]; b1 = F[1]; b2 = F[2]; b3 = F[3]

  // Notes on the sheet:
  //   Arrumar essa poha aqui
endmodule

// 30
module Registradores (
  input  [4:0] A1,
  input  [15:0] D,
  input  E,
  input  C,
  input  R,
  input  [4:0] A2,
  output [15:0] O1,
  output [15:0] O2
);

  wire and_1_out, and_2_out, and_3_out, and_4_out, and_5_out, and_6_out, and_7_out, and_8_out, and_9_out,
       and_10_out, and_11_out, and_12_out, and_13_out, and_14_out, and_15_out, and_16_out, and_17_out,
       and_18_out, and_19_out, and_20_out, and_21_out, and_22_out, and_23_out, and_24_out, and_25_out,
       and_26_out, and_27_out, and_28_out, and_29_out, and_30_out, and_31_out, and_32_out, decoder_1_out0,
       decoder_1_out1, decoder_1_out2, decoder_1_out3, decoder_1_out4, decoder_1_out5, decoder_1_out6,
       decoder_1_out7, decoder_1_out8, decoder_1_out9, decoder_1_out10, decoder_1_out11, decoder_1_out12,
       decoder_1_out13, decoder_1_out14, decoder_1_out15, decoder_1_out16, decoder_1_out17, decoder_1_out18,
       decoder_1_out19, decoder_1_out20, decoder_1_out21, decoder_1_out22, decoder_1_out23, decoder_1_out24,
       decoder_1_out25, decoder_1_out26, decoder_1_out27, decoder_1_out28, decoder_1_out29, decoder_1_out30,
       decoder_1_out31;
  wire [15:0] _00, _01, _02, _03, _04, _05, _06, _07, _08, _09, _10, _11, _12, _13, _14, _15, _16, _17, _18,
       _19, _20, _21, _22, _23, _24, _25, _26, _27, _28, _29, _30, _31;

  Decoder #(.select(5)) decoder_1 (
    .out0(decoder_1_out0), .out1(decoder_1_out1), .out2(decoder_1_out2), .out3(decoder_1_out3),
    .out4(decoder_1_out4), .out5(decoder_1_out5), .out6(decoder_1_out6), .out7(decoder_1_out7),
    .out8(decoder_1_out8), .out9(decoder_1_out9), .out10(decoder_1_out10), .out11(decoder_1_out11),
    .out12(decoder_1_out12), .out13(decoder_1_out13), .out14(decoder_1_out14), .out15(decoder_1_out15),
    .out16(decoder_1_out16), .out17(decoder_1_out17), .out18(decoder_1_out18), .out19(decoder_1_out19),
    .out20(decoder_1_out20), .out21(decoder_1_out21), .out22(decoder_1_out22), .out23(decoder_1_out23),
    .out24(decoder_1_out24), .out25(decoder_1_out25), .out26(decoder_1_out26), .out27(decoder_1_out27),
    .out28(decoder_1_out28), .out29(decoder_1_out29), .out30(decoder_1_out30), .out31(decoder_1_out31),
    .sel(A1));  // open: en
  and and_1 (and_1_out, decoder_1_out0, E);
  Register #(.width(16)) register_1 (.D(D), .en(and_1_out), .Q(_00), .clk(C), .clr(R));
  Register #(.width(16)) register_2 (.D(D), .en(and_2_out), .Q(_01), .clk(C), .clr(R));
  and and_2 (and_2_out, decoder_1_out1, E);
  and and_3 (and_3_out, decoder_1_out2, E);
  SuperMux supermux_1 (
    .in_1(_31), .in_2(_30), .in_3(_29), .in_4(_28), .in_5(_27), .in_6(_26), .in_7(_25), .in_8(_24),
    .in_10(_23), .in_11(_22), .in_12(_21), .in_13(_20), .in_14(_19), .in_15(_18), .in_16(_17), .in_17(_16),
    .in_18(_15), .in_19(_14), .in_20(_13), .in_21(_12), .in_22(_11), .in_24(_10), .in_25(_09), .in_26(_08),
    .in_27(_07), .in_28(_06), .in_29(_05), .in_30(_04), .in_31(_03), .in_32(_02), .in_33(_01), .in_34(_00),
    .in_9(A1), .in_23(A2), .out_35(O2), .out_36(O1));
  Register #(.width(16)) register_3 (.D(D), .en(and_3_out), .Q(_02), .clk(C), .clr(R));
  Register #(.width(16)) register_4 (.D(D), .en(and_4_out), .Q(_03), .clk(C), .clr(R));
  and and_4 (and_4_out, decoder_1_out3, E);
  and and_5 (and_5_out, decoder_1_out4, E);
  Register #(.width(16)) register_5 (.D(D), .en(and_5_out), .Q(_04), .clk(C), .clr(R));
  Register #(.width(16)) register_6 (.D(D), .en(and_6_out), .Q(_05), .clk(C), .clr(R));
  and and_6 (and_6_out, decoder_1_out5, E);
  and and_7 (and_7_out, decoder_1_out6, E);
  Register #(.width(16)) register_7 (.D(D), .en(and_7_out), .Q(_06), .clk(C), .clr(R));
  Register #(.width(16)) register_8 (.D(D), .en(and_8_out), .Q(_07), .clk(C), .clr(R));
  and and_8 (and_8_out, decoder_1_out7, E);
  and and_9 (and_9_out, decoder_1_out8, E);
  Register #(.width(16)) register_9 (.D(D), .en(and_9_out), .Q(_08), .clk(C), .clr(R));
  Register #(.width(16)) register_10 (.D(D), .en(and_10_out), .Q(_09), .clk(C), .clr(R));
  and and_10 (and_10_out, decoder_1_out9, E);
  and and_11 (and_11_out, decoder_1_out10, E);
  Register #(.width(16)) register_11 (.D(D), .en(and_11_out), .Q(_10), .clk(C), .clr(R));
  Register #(.width(16)) register_12 (.D(D), .en(and_12_out), .Q(_11), .clk(C), .clr(R));
  and and_12 (and_12_out, decoder_1_out11, E);
  and and_13 (and_13_out, decoder_1_out12, E);
  Register #(.width(16)) register_13 (.D(D), .en(and_13_out), .Q(_12), .clk(C), .clr(R));
  Register #(.width(16)) register_14 (.D(D), .en(and_14_out), .Q(_13), .clk(C), .clr(R));
  and and_14 (and_14_out, decoder_1_out13, E);
  Register #(.width(16)) register_15 (.D(D), .en(and_15_out), .Q(_14), .clk(C), .clr(R));
  and and_15 (and_15_out, decoder_1_out14, E);
  and and_16 (and_16_out, decoder_1_out15, E);
  Register #(.width(16)) register_16 (.D(D), .en(and_16_out), .Q(_15), .clk(C), .clr(R));
  Register #(.width(16)) register_17 (.D(D), .en(and_17_out), .Q(_16), .clk(C), .clr(R));
  and and_17 (and_17_out, decoder_1_out16, E);
  and and_18 (and_18_out, decoder_1_out17, E);
  Register #(.width(16)) register_18 (.D(D), .en(and_18_out), .Q(_17), .clk(C), .clr(R));
  Register #(.width(16)) register_19 (.D(D), .en(and_19_out), .Q(_18), .clk(C), .clr(R));
  and and_19 (and_19_out, decoder_1_out18, E);
  and and_20 (and_20_out, decoder_1_out19, E);
  Register #(.width(16)) register_20 (.D(D), .en(and_20_out), .Q(_19), .clk(C), .clr(R));
  Register #(.width(16)) register_21 (.D(D), .en(and_21_out), .Q(_20), .clk(C), .clr(R));
  and and_21 (and_21_out, decoder_1_out20, E);
  and and_22 (and_22_out, decoder_1_out21, E);
  Register #(.width(16)) register_22 (.D(D), .en(and_22_out), .Q(_21), .clk(C), .clr(R));
  Register #(.width(16)) register_23 (.D(D), .en(and_23_out), .Q(_22), .clk(C), .clr(R));
  and and_23 (and_23_out, decoder_1_out22, E);
  and and_24 (and_24_out, decoder_1_out23, E);
  Register #(.width(16)) register_24 (.D(D), .en(and_24_out), .Q(_23), .clk(C), .clr(R));
  Register #(.width(16)) register_25 (.D(D), .en(and_25_out), .Q(_24), .clk(C), .clr(R));
  and and_25 (and_25_out, decoder_1_out24, E);
  and and_26 (and_26_out, decoder_1_out25, E);
  Register #(.width(16)) register_26 (.D(D), .en(and_26_out), .Q(_25), .clk(C), .clr(R));
  Register #(.width(16)) register_27 (.D(D), .en(and_27_out), .Q(_26), .clk(C), .clr(R));
  and and_27 (and_27_out, decoder_1_out26, E);
  and and_28 (and_28_out, decoder_1_out27, E);
  Register #(.width(16)) register_28 (.D(D), .en(and_28_out), .Q(_27), .clk(C), .clr(R));
  Register #(.width(16)) register_29 (.D(D), .en(and_29_out), .Q(_28), .clk(C), .clr(R));
  and and_29 (and_29_out, decoder_1_out28, E);
  and and_30 (and_30_out, decoder_1_out29, E);
  Register #(.width(16)) register_30 (.D(D), .en(and_30_out), .Q(_29), .clk(C), .clr(R));
  and and_31 (and_31_out, decoder_1_out30, E);
  Register #(.width(16)) register_31 (.D(D), .en(and_31_out), .Q(_30), .clk(C), .clr(R));
  Register #(.width(16)) register_32 (.D(D), .en(and_32_out), .Q(_31), .clk(C), .clr(R));
  and and_32 (and_32_out, decoder_1_out31, E);
endmodule

module SuperMux (
  input  [15:0] in_1,
  input  [15:0] in_2,
  input  [15:0] in_3,
  input  [15:0] in_4,
  input  [15:0] in_5,
  input  [15:0] in_6,
  input  [15:0] in_7,
  input  [15:0] in_8,
  input  [4:0] in_9,
  input  [15:0] in_10,
  input  [15:0] in_11,
  input  [15:0] in_12,
  input  [15:0] in_13,
  input  [15:0] in_14,
  input  [15:0] in_15,
  input  [15:0] in_16,
  input  [15:0] in_17,
  input  [15:0] in_18,
  input  [15:0] in_19,
  input  [15:0] in_20,
  input  [15:0] in_21,
  input  [15:0] in_22,
  input  [4:0] in_23,
  input  [15:0] in_24,
  input  [15:0] in_25,
  input  [15:0] in_26,
  input  [15:0] in_27,
  input  [15:0] in_28,
  input  [15:0] in_29,
  input  [15:0] in_30,
  input  [15:0] in_31,
  input  [15:0] in_32,
  input  [15:0] in_33,
  input  [15:0] in_34,
  output [15:0] out_35,
  output [15:0] out_36
);

  Multiplexer #(.select(5), .width(16)) multiplexer_1 (
    .in0(in_34), .in1(in_33), .in2(in_32), .in3(in_31), .in4(in_30), .in5(in_29), .in6(in_28), .in7(in_27),
    .in8(in_26), .in9(in_25), .in10(in_24), .in11(in_22), .in12(in_21), .in13(in_20), .in14(in_19),
    .in15(in_18), .in16(in_17), .in17(in_16), .in18(in_15), .in19(in_14), .in20(in_13), .in21(in_12),
    .in22(in_11), .in23(in_10), .in24(in_8), .in25(in_7), .in26(in_6), .in27(in_5), .in28(in_4), .in29(in_3),
    .in30(in_2), .in31(in_1), .out(out_35), .sel(in_9));  // open: en
  Multiplexer #(.select(5), .width(16)) multiplexer_2 (
    .in0(in_34), .in1(in_33), .in2(in_32), .in3(in_31), .in4(in_30), .in5(in_29), .in6(in_28), .in7(in_27),
    .in8(in_26), .in9(in_25), .in10(in_24), .in11(in_22), .in12(in_21), .in13(in_20), .in14(in_19),
    .in15(in_18), .in16(in_17), .in17(in_16), .in18(in_15), .in19(in_14), .in20(in_13), .in21(in_12),
    .in22(in_11), .in23(in_10), .in24(in_8), .in25(in_7), .in26(in_6), .in27(in_5), .in28(in_4), .in29(in_3),
    .in30(in_2), .in31(in_1), .out(out_36), .sel(in_23));  // open: en

  // Other names for the same wires on the sheet: _00[15:0] = in_34; _01[15:0] = in_33; _02[15:0] = in_32;
  //   _03[15:0] = in_31; _04[15:0] = in_30; _05[15:0] = in_29; _06[15:0] = in_28; _07[15:0] = in_27;
  //   _08[15:0] = in_26; _09[15:0] = in_25; _10[15:0] = in_24; _11[15:0] = in_22; _12[15:0] = in_21;
  //   _13[15:0] = in_20; _14[15:0] = in_19; _15[15:0] = in_18; _16[15:0] = in_17; _17[15:0] = in_16;
  //   _18[15:0] = in_15; _19[15:0] = in_14; _20[15:0] = in_13; _21[15:0] = in_12; _22[15:0] = in_11;
  //   _23[15:0] = in_10; _24[15:0] = in_8; _25[15:0] = in_7; _26[15:0] = in_6; _27[15:0] = in_5; _28[15:0] = in_4;
  //   _29[15:0] = in_3; _30[15:0] = in_2; _31[15:0] = in_1
endmodule

module Processor (
  input  reset,
  input  clock,
  input  [15:0] ins,
  output [11:0] out_4,
  output [15:0] S1,
  output [15:0] S2,
  output [15:0] SA,
  output [15:0] SE
);

  wire add, \and , and_15_out, and_16_out, and_17_out, and_22_out, and_23_out, and_24_out, and_25_out,
       and_26_out, call, cmp, cmp_flag_e, cmp_flag_g, comparator_1_eq, comparator_2_eq, comparator_3_eq,
       comparator_4_eq, div, En, Fle, Flg, je, jg, jmp, jne, loa, mov, movcons, mul, \not , not_1_out,
       not_2_out, not_3_out, not_4_out, not_5_out, not_6_out, not_7_out, not_8_out, not_9_out, not_10_out,
       not_11_out, not_12_out, not_13_out, not_14_out, not_15_out, not_16_out, not_17_out, not_18_out,
       not_19_out, not_20_out, not_21_out, not_22_out, not_23_out, not_24_out, not_25_out, not_26_out,
       not_27_out, not_28_out, not_29_out, not_30_out, not_31_out, not_32_out, not_33_out, not_34_out,
       not_35_out, not_36_out, not_37_out, not_38_out, not_39_out, not_40_out, not_41_out, not_42_out,
       not_43_out, not_44_out, not_45_out, not_47_out, not_48_out, not_49_out, not_50_out, \or , or_1_out,
       or_2_out, or_5_out, pc_count, pc_load, ret, shl, shr, stack_count, str, sub;
  wire [1:0] not_51_out;
  wire [4:0] Add1;
  wire [11:0] adder_1_out, pc_data, stackout;
  wire [15:0] A, B, bit_extender_1_out, Data, memoryout, multiplexer_1_out, Res, stack, subtractor_1_out;

  not not_1 (not_1_out, ins[10]);
  not not_2 (not_2_out, ins[14]);
  not not_3 (not_3_out, ins[13]);
  not not_4 (not_4_out, ins[14]);
  not not_5 (not_5_out, ins[10]);
  not not_6 (not_6_out, ins[11]);
  not not_7 (not_7_out, ins[12]);
  not not_8 (not_8_out, ins[14]);
  not not_9 (not_9_out, ins[15]);
  not not_10 (not_10_out, ins[11]);
  not not_11 (not_11_out, ins[12]);
  not not_12 (not_12_out, ins[14]);
  not not_13 (not_13_out, ins[15]);
  not not_14 (not_14_out, ins[10]);
  not not_15 (not_15_out, ins[12]);
  not not_16 (not_16_out, ins[14]);
  not not_17 (not_17_out, ins[15]);
  not not_18 (not_18_out, ins[12]);
  not not_19 (not_19_out, ins[14]);
  not not_20 (not_20_out, ins[15]);
  not not_21 (not_21_out, ins[10]);
  not not_22 (not_22_out, ins[11]);
  not not_23 (not_23_out, ins[14]);
  not not_24 (not_24_out, ins[15]);
  not not_25 (not_25_out, ins[11]);
  not not_26 (not_26_out, ins[14]);
  not not_27 (not_27_out, ins[15]);
  not not_28 (not_28_out, ins[10]);
  not not_29 (not_29_out, ins[14]);
  not not_30 (not_30_out, ins[15]);
  and and_1 (\or , ins[10], ins[11], ins[12], not_31_out, not_32_out, ins[13]);
  not not_31 (not_31_out, ins[14]);
  not not_32 (not_32_out, ins[15]);
  not not_33 (not_33_out, ins[10]);
  not not_34 (not_34_out, ins[12]);
  and and_2 (\not , not_33_out, ins[11], not_34_out, not_35_out, ins[15], ins[13]);
  not not_35 (not_35_out, ins[14]);
  not not_36 (not_36_out, ins[11]);
  not not_37 (not_37_out, ins[12]);
  and and_3 (mov, not_1_out, not_36_out, not_37_out, not_2_out, ins[15], ins[13]);
  Subtractor #(.width(16)) subtractor_1 (.a(stack), .b(16'h1), .out(subtractor_1_out));  // open: bin, bout
  and and_4 (movcons, not_3_out, not_4_out, ins[15]);
  and and_5 (add, not_5_out, not_6_out, not_7_out, not_8_out, not_9_out, ins[13]);
  and and_6 (sub, ins[10], not_10_out, not_11_out, not_12_out, not_13_out, ins[13]);
  and and_7 (mul, not_14_out, ins[11], not_15_out, not_16_out, not_17_out, ins[13]);
  and and_8 (div, ins[10], ins[11], not_18_out, not_19_out, not_20_out, ins[13]);
  and and_9 (shl, not_21_out, not_22_out, ins[12], not_23_out, not_24_out, ins[13]);
  and and_10 (shr, ins[10], not_25_out, ins[12], not_26_out, not_27_out, ins[13]);
  and and_11 (\and , not_28_out, ins[11], ins[12], not_29_out, not_30_out, ins[13]);
  Counter #(.width(12), .max('hfff)) counter_1 (
    .load(pc_load), .D(pc_data), .count(pc_count), .Q(out_4), .clk(clock), .clr(reset));  // open: carry
  not not_38 (not_38_out, ins[10]);
  not not_39 (not_39_out, ins[11]);
  not not_40 (not_40_out, ins[13]);
  not not_41 (not_41_out, ins[15]);
  not not_42 (not_42_out, ins[10]);
  not not_43 (not_43_out, ins[11]);
  not not_44 (not_44_out, ins[15]);
  Multiplexer #(.width(16)) multiplexer_1 (
    .in0(stack), .in1(subtractor_1_out), .out(multiplexer_1_out), .sel(ret));  // open: en
  Counter #(.width(16), .max('hffff)) counter_2 (
    .load(ret), .count(stack_count), .Q(stack), .clk(clock), .clr(reset));  // open: D, carry
  and and_12 (loa, not_38_out, not_39_out, ins[12], ins[14], not_41_out, not_40_out);
  and and_13 (str, not_42_out, not_43_out, ins[12], ins[14], not_44_out, ins[13]);
  and and_14 (je, ~ins[12], ~ins[13], ins[14], ins[15]);  // AND_Gate
  or or_1 (or_1_out, ret, call);
  Register #(.width(1)) register_1 (.D(Flg), .en(cmp), .Q(cmp_flag_g), .clk(clock), .clr(reset));
  Register #(.width(1)) register_2 (.D(Fle), .en(cmp), .Q(cmp_flag_e), .clk(clock), .clr(reset));
  and and_15 (and_15_out, je, cmp_flag_e);
  and and_16 (and_16_out, jne, not_45_out);
  not not_45 (not_45_out, cmp_flag_e);
  and and_17 (and_17_out, jg, cmp_flag_g);
  // Probe on pc_data
  or or_2 (or_2_out, loa, str);
  and and_18 (cmp, ins[10], ~ins[11], ~ins[12], ins[13], ~ins[14], ins[15]);  // AND_Gate
  Multiplexer #(.width(12)) multiplexer_2 (.in0(ins[11:0]), .in1(stackout), .out(pc_data), .sel(ret));  // open: en
  // Probe on memoryout
  RAM #(.addrWidth(16), .dataWidth(16)) ram_1 (
    .addr(B), .data(memoryout), .sel(or_2_out), .clk(clock), .ld(loa), .clr(reset));
  RAM #(.addrWidth(16), .dataWidth(12)) ram_2 (
    .addr(multiplexer_1_out), .data(stackout), .sel(or_1_out), .clk(clock), .ld(ret), .clr(reset));
  Registradores registradores_1 (.D(Data), .E(En), .C(clock), .R(reset), .A2(ins[4:0]), .O1(B), .O2(A), .A1(Add1));
  or or_3 (pc_load, ret, jmp, and_15_out, and_16_out, and_17_out, call);
  and and_19 (jmp, ins[12], ins[13], ins[14], ins[15]);
  and and_20 (jg, ~ins[12], ins[13], ins[14], ins[15]);  // AND_Gate
  and and_21 (jne, ins[12], ~ins[13], ins[14], ins[15]);  // AND_Gate
  ULA ula_1 (.A(A), .F(ins[13:10]), .B(B), .R(Res), .FG(Flg), .FE(Fle));
  Multiplexer #(.width(5)) multiplexer_3 (.in0(ins[9:5]), .in1(ins[4:0]), .out(Add1), .sel(movcons));  // open: en
  not not_46 (pc_count, pc_load);
  Adder #(.width(12)) adder_1 (.a(out_4), .b(12'h1), .out(adder_1_out));  // open: cin, cout
  // Probe on memoryout
  Multiplexer #(.width(16)) multiplexer_4 (.in0(A), .out(memoryout), .sel(loa));  // open: in1, en
  Comparator #(.width(16), .mode("unsigned")) comparator_1 (.a(16'hea61), .b(B), .eq(comparator_1_eq));  // open: gt, lt
  Comparator #(.width(16), .mode("unsigned")) comparator_2 (.a(16'hea62), .b(B), .eq(comparator_2_eq));  // open: gt, lt
  Comparator #(.width(16), .mode("unsigned")) comparator_3 (.a(16'hea63), .b(B), .eq(comparator_3_eq));  // open: gt, lt
  // Probe on stackout
  Multiplexer #(.width(12)) multiplexer_5 (.in0(adder_1_out), .out(stackout), .sel(ret));  // open: in1, en
  // Probe on Data
  // Probe on Add1
  // Probe on ins[4:0]
  // Probe on A
  // Probe on B
  // Probe on ins[13:10]
  // Probe on Res
  Comparator #(.width(16), .mode("unsigned")) comparator_4 (.a(16'hea60), .b(B), .eq(comparator_4_eq));  // open: gt, lt
  and and_22 (and_22_out, comparator_4_eq, str);
  and and_23 (and_23_out, comparator_1_eq, str);
  and and_24 (and_24_out, comparator_2_eq, str);
  and and_25 (and_25_out, comparator_3_eq, str);
  or or_4 (En, movcons, sub, add, mul, div, shl, shr, \and , \or , \not , mov, loa);
  assign bit_extender_1_out = {{8{1'b0}}, ins[12:5]};  // Bit_Extender bit_extender_1
  not not_47 (not_47_out, movcons);
  and and_26 (and_26_out, not_47_out, mov);
  or or_5 (or_5_out, movcons, mov);
  Register #(.width(16)) register_3 (.D(memoryout), .en(and_22_out), .Q(S1), .clk(clock), .clr(reset));
  Register #(.width(16)) register_4 (.D(memoryout), .en(and_23_out), .Q(S2), .clk(clock), .clr(reset));
  Register #(.width(16)) register_5 (.D(memoryout), .en(and_24_out), .Q(SA), .clk(clock), .clr(reset));
  Register #(.width(16)) register_6 (.D(memoryout), .en(and_25_out), .Q(SE), .clk(clock), .clr(reset));
  not not_48 (not_48_out, ins[14]);
  not not_49 (not_49_out, ins[12]);
  not not_50 (not_50_out, ins[14]);
  or or_6 (not_51_out[1], loa, and_26_out);
  not not_51 (not_51_out[0], or_5_out);
  and and_27 (call, ins[12], not_48_out, ins[15], ins[13]);
  and and_28 (ret, ins[10], ins[11], not_49_out, not_50_out, ins[15], ins[13]);
  or or_7 (stack_count, ret, call);
  // Probe on Data
  Multiplexer #(.select(2), .width(16)) multiplexer_6 (
    .in0(bit_extender_1_out), .in1(Res), .in2(B), .in3(memoryout), .out(Data), .sel(not_51_out));  // open: en

  // Other names for the same wires on the sheet: clk = clock; con[7:0] = ins[12:5]; label[11:0] = ins[11:0];
  //   Op[3:0] = ins[13:10]; pc[11:0] = out_4; Q1[15:0] = A; Q2[15:0] = B; reg1[4:0] = ins[9:5]; Add2[4:0] = ins[4:0];
  //   reg2[4:0] = ins[4:0]; Rs = reset; stack_load = ret

  // Notes on the sheet:
  //   RISC Lukitias
endmodule
