// Logisim project screenbufferimpl.circ as structural Verilog: 2 circuits, main circuit main
module main (
  input  [4:0] in_1,
  input  [31:0] in_2,
  input  in_3,
  input  in_4
);

  wire clock_1_out;
  wire [31:0] screenbuffer_1_out_6, screenbuffer_1_out_7, screenbuffer_1_out_8, screenbuffer_1_out_9,
       screenbuffer_1_out_10, screenbuffer_1_out_11, screenbuffer_1_out_12, screenbuffer_1_out_13,
       screenbuffer_1_out_14, screenbuffer_1_out_15, screenbuffer_1_out_16, screenbuffer_1_out_17,
       screenbuffer_1_out_18, screenbuffer_1_out_19, screenbuffer_1_out_20, screenbuffer_1_out_21,
       screenbuffer_1_out_22, screenbuffer_1_out_23, screenbuffer_1_out_24, screenbuffer_1_out_25,
       screenbuffer_1_out_26, screenbuffer_1_out_27, screenbuffer_1_out_28, screenbuffer_1_out_29,
       screenbuffer_1_out_30, screenbuffer_1_out_31, screenbuffer_1_out_32, screenbuffer_1_out_33,
       screenbuffer_1_out_34, screenbuffer_1_out_35, screenbuffer_1_out_36, screenbuffer_1_out_37;

  DotMatrix #(.matrixcols(32), .matrixrows(32), .persist(64)) dotmatrix_1 (
    .col0(screenbuffer_1_out_6), .col1(screenbuffer_1_out_7), .col2(screenbuffer_1_out_8),
    .col3(screenbuffer_1_out_9), .col4(screenbuffer_1_out_10), .col5(screenbuffer_1_out_11),
    .col6(screenbuffer_1_out_12), .col7(screenbuffer_1_out_13), .col8(screenbuffer_1_out_14),
    .col9(screenbuffer_1_out_15), .col10(screenbuffer_1_out_16), .col11(screenbuffer_1_out_17),
    .col12(screenbuffer_1_out_18), .col13(screenbuffer_1_out_19), .col14(screenbuffer_1_out_20),
    .col15(screenbuffer_1_out_21), .col16(screenbuffer_1_out_37), .col17(screenbuffer_1_out_36),
    .col18(screenbuffer_1_out_35), .col19(screenbuffer_1_out_34), .col20(screenbuffer_1_out_33),
    .col21(screenbuffer_1_out_32), .col22(screenbuffer_1_out_31), .col23(screenbuffer_1_out_30),
    .col24(screenbuffer_1_out_29), .col25(screenbuffer_1_out_28), .col26(screenbuffer_1_out_27),
    .col27(screenbuffer_1_out_26), .col28(screenbuffer_1_out_25), .col29(screenbuffer_1_out_24),
    .col30(screenbuffer_1_out_23), .col31(screenbuffer_1_out_22));
  screenbuffer screenbuffer_1 (
    .Address(in_1), .data(in_2), .enable(in_3), .clock(clock_1_out), .clear(in_4),
    .out_6(screenbuffer_1_out_6), .out_7(screenbuffer_1_out_7), .out_8(screenbuffer_1_out_8),
    .out_9(screenbuffer_1_out_9), .out_10(screenbuffer_1_out_10), .out_11(screenbuffer_1_out_11),
    .out_12(screenbuffer_1_out_12), .out_13(screenbuffer_1_out_13), .out_14(screenbuffer_1_out_14),
    .out_15(screenbuffer_1_out_15), .out_16(screenbuffer_1_out_16), .out_17(screenbuffer_1_out_17),
    .out_18(screenbuffer_1_out_18), .out_19(screenbuffer_1_out_19), .out_20(screenbuffer_1_out_20),
    .out_21(screenbuffer_1_out_21), .out_22(screenbuffer_1_out_22), .out_23(screenbuffer_1_out_23),
    .out_24(screenbuffer_1_out_24), .out_25(screenbuffer_1_out_25), .out_26(screenbuffer_1_out_26),
    .out_27(screenbuffer_1_out_27), .out_28(screenbuffer_1_out_28), .out_29(screenbuffer_1_out_29),
    .out_30(screenbuffer_1_out_30), .out_31(screenbuffer_1_out_31), .out_32(screenbuffer_1_out_32),
    .out_33(screenbuffer_1_out_33), .out_34(screenbuffer_1_out_34), .out_35(screenbuffer_1_out_35),
    .out_36(screenbuffer_1_out_36), .out_37(screenbuffer_1_out_37));
  Clock clock_1 (.out(clock_1_out));
endmodule

module screenbuffer (
  input  [4:0] Address,
  input  [31:0] data,
  input  enable,
  input  clock,
  input  clear,
  output [31:0] out_6,
  output [31:0] out_7,
  output [31:0] out_8,
  output [31:0] out_9,
  output [31:0] out_10,
  output [31:0] out_11,
  output [31:0] out_12,
  output [31:0] out_13,
  output [31:0] out_14,
  output [31:0] out_15,
  output [31:0] out_16,
  output [31:0] out_17,
  output [31:0] out_18,
  output [31:0] out_19,
  output [31:0] out_20,
  output [31:0] out_21,
  output [31:0] out_22,
  output [31:0] out_23,
  output [31:0] out_24,
  output [31:0] out_25,
  output [31:0] out_26,
  output [31:0] out_27,
  output [31:0] out_28,
  output [31:0] out_29,
  output [31:0] out_30,
  output [31:0] out_31,
  output [31:0] out_32,
  output [31:0] out_33,
  output [31:0] out_34,
  output [31:0] out_35,
  output [31:0] out_36,
  output [31:0] out_37
);

  wire not_1_out, not_2_out;
  wire [4:0] counter_1_q, multiplexer_1_out;
  wire [31:0] ram_1_data, ram_2_data;

  Multiplexer #(.width(5)) multiplexer_1 (
    .in0(counter_1_q), .in1(Address), .out(multiplexer_1_out), .sel(enable));  // open: en
  RAM #(.addrWidth(5), .dataWidth(32), .bus("separate")) ram_1 (
    .addr(multiplexer_1_out), .din(data), .data(ram_1_data), .str(enable), .clk(clock), .ld(not_1_out),
    .clr(clear));  // open: sel
  not not_1 (not_1_out, enable);
  Counter #(.width(5), .max('h1f)) counter_1 (
    .Q(counter_1_q), .clk(clock), .clr(clear));  // open: load, D, count, carry
  RAM #(.addrWidth(5), .dataWidth(32), .bus("separate")) ram_2 (
    .addr(counter_1_q), .din(ram_1_data), .data(ram_2_data), .str(not_1_out), .clk(clock), .clr(clear));  // open: sel, ld
  Demultiplexer #(.select(5), .width(32), .disabled(0)) demultiplexer_1 (
    .out0(out_6), .out1(out_7), .out2(out_8), .out3(out_9), .out4(out_10), .out5(out_11), .out6(out_12),
    .out7(out_13), .out8(out_14), .out9(out_15), .out10(out_16), .out11(out_17), .out12(out_18),
    .out13(out_19), .out14(out_20), .out15(out_21), .out16(out_37), .out17(out_36), .out18(out_35),
    .out19(out_34), .out20(out_33), .out21(out_32), .out22(out_31), .out23(out_30), .out24(out_29),
    .out25(out_28), .out26(out_27), .out27(out_26), .out28(out_25), .out29(out_24), .out30(out_23),
    .out31(out_22), .in(ram_2_data), .sel(counter_1_q), .en(not_2_out));
  not not_2 (not_2_out, clock);
endmodule
